# Fritzing sketch gyro (saved by Fritzing 1.0.8)
breadboards: 1

parts:
  M1 = gy9250
  MCU1 = Raspberry Pi Zero

nets:
  N1: M1.pin1, MCU1.pin_1
  N2: M1.pin2, MCU1.pin_6, MCU1.pin_9
  N3: M1.pin3, MCU1.pin_5
  N4: M1.pin4, MCU1.pin_3

custom parts:
  gy9250: MPU-9250 module (three-axis gyroscope + three-axis acceleration + three-axis magnetic field). The generic model from ebay et. al. rather than the Sparkfun version.
