# Fritzing sketch lab2 (saved by Fritzing 1.0.8)
circuit board: 9.906cm x 7.493cm
breadboards: 1

parts:
  MCU1 = Raspberry Pi Zero
  OLED1 = OLED 128x64 I2C Monochrome Display VDD-GND
  Part1 = Adafruit TCS34725 RGB Color Sensor [part_number="Adafruit #1334"]

nets:
  VDD: MCU1.pin_1, MCU1.pin_17, OLED1.VDD, Part1.VIN
  N1: MCU1.pin_3, OLED1.SDA, Part1.SDA
  N2: MCU1.pin_5, OLED1.SCK, Part1.SCL
  GND: MCU1.pin_9, MCU1.pin_39, OLED1.GND, Part1.GND

custom parts:
  OLED 128x64 I2C Monochrome Display VDD-GND: OLED 128x64 I2C Monochrome Display. Note: there are two variants of this part, this one is the VDD GND SCK SDA variant. The other is GND VDD SCK SDA. Make sure you select the part that matches your module as using the incorrect part will probably destroy your module! In addition the mounting holes are marked on silkscreen but not by default drilled. If you want drilled mounting holes, copy a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
