# Fritzing sketch motor-wiring (saved by Fritzing 1.0.8)

parts:
  Pi_Zero_W = Raspberry Pi Zero
  RovMotPow = RovMotPow power/motor board A.4 with DRV8833 in U2
  Motor_A = Micro metal gearmotor 50:1 with encoder (Motor A (left))
  Motor_B = Micro metal gearmotor 50:1 with encoder (Motor B (right))
  LM2596 = LM2596S buck converter (5.1 V)
  HUSB238 = HUSB238 USB-C PD trigger (9 V)
  Power_bank = USB-C PD power bank 10 Ah

nets:
  N1: Pi_Zero_W.pin_2, RovMotPow.J10_5VIN+, RovMotPow.J2.1_5V, LM2596.OUT+
  GND: Pi_Zero_W.pin_6, RovMotPow.J3.5_GND, RovMotPow.J6.5_GND, RovMotPow.J9_7VOUT-, RovMotPow.J10_5VIN-, RovMotPow.J1_BAT-, RovMotPow.J2.3_GND, Motor_A.GND, Motor_B.GND, LM2596.IN-, LM2596.OUT-, HUSB238.GND
  N2: Pi_Zero_W.pin_12, RovMotPow.J5.2_AIN2
  N3: Pi_Zero_W.pin_13, RovMotPow.J5.3_AENC2, RovMotPow.J3.3_C2, Motor_A.C2
  N4: Pi_Zero_W.pin_15, RovMotPow.J5.4_AENC1, RovMotPow.J3.4_C1, Motor_A.C1
  VCC: Pi_Zero_W.pin_17, RovMotPow.J3.2_VCC, RovMotPow.J6.2_VCC, RovMotPow.J12.1_3V3, Motor_A.VCC, Motor_B.VCC
  N5: Pi_Zero_W.pin_29, RovMotPow.J8.3_BENC2, RovMotPow.J6.3_C2, Motor_B.C2
  N6: Pi_Zero_W.pin_32, RovMotPow.J5.1_AIN1
  N7: Pi_Zero_W.pin_33, RovMotPow.J8.1_BIN1
  N8: Pi_Zero_W.pin_35, RovMotPow.J8.2_BIN2
  N9: Pi_Zero_W.pin_37, RovMotPow.J12.3_SLP
  N10: Pi_Zero_W.pin_40, RovMotPow.J8.4_BENC1, RovMotPow.J6.4_C1, Motor_B.C1
  N11: RovMotPow.J3.1_M2, Motor_A.M2
  N12: RovMotPow.J3.6_M1, Motor_A.M1
  N13: RovMotPow.J6.1_M2, Motor_B.M2
  N14: RovMotPow.J6.6_M1, Motor_B.M1
  N15: RovMotPow.J9_7VOUT+, LM2596.IN+
  N16: RovMotPow.J1_BAT+, HUSB238.VOUT
  N17: HUSB238.USB-C, Power_bank.USB-C

notes:
  Rover motor wiring (Lab 5)
  Motor cable (JST-ZH into J3 / J6): M2 red = Motor+, VCC black = Encoder+ 3.3 V, C2 yellow = Enc A, C1 green = Enc B, GND blue, M1 white = Motor-.
  DRV8833 sits in U2: AOUT1 / AOUT2 → motor A M2 / M1, BOUT1 / BOUT2 → motor B M2 / M1. Swapping M1 and M2 only reverses the wheel.
  Pi Zero W: MOTA J5: 1 AIN1 = GPIO12, 2 AIN2 = GPIO18, 3 C2 = GPIO27, 4 C1 = GPIO22. MOTB J8: 1 BIN1 = GPIO13, 2 BIN2 = GPIO19, 3 C2 = GPIO5, 4 C1 = GPIO21. J12 SLP = GPIO26 (or jumper SLP to 3V3). J12 3V3 is fed from Pi pin 17 (3V3) and powers both encoders - the board has no 3.3 V regulator. PIPOW 5V / GND → Pi pin 2 / pin 6.
  Power: USB-C power bank → HUSB238 (9 V) → J1 BAT → SW1 → 7V2 rail (DRV8833 VM and J9 7VOUT) → LM2596 (5.1 V) → J10 5VIN → PIPOW.
  Pin numbers follow the board schematic; the Canvas Lab 5 table lists MOTA 3 = C1 / 4 = C2 and AOUT1 = M1 (swapped), which only flips wheel / encoder direction in code.

custom parts:
  RovMotPow power/motor board A.4 with DRV8833 in U2: CPSY rover power distribution / motor board (RoverMotorPower.SchDoc, J. T. Foley) with a DRV8833 breakout plugged into U2. Buses follow the schematic; U2 pins are internal to this part.
  Micro metal gearmotor 50:1 with encoder (Motor A (left)): Kit motor: Micro Metal Geared motor w/Encoder 12V 300RPM 50:1, 6-pin JST-ZH: M2 red Motor+, VCC black Encoder+, C2 yellow Enc A, C1 green Enc B, GND blue, M1 white Motor-.
  Micro metal gearmotor 50:1 with encoder (Motor B (right)): Kit motor: Micro Metal Geared motor w/Encoder 12V 300RPM 50:1, 6-pin JST-ZH: M2 red Motor+, VCC black Encoder+, C2 yellow Enc A, C1 green Enc B, GND blue, M1 white Motor-.
  LM2596S buck converter (5.1 V): LM2596 DC/DC module, output trimmed to 5.1-5.2 V. IN from J9 7VOUT, OUT to J10 5VIN.
  HUSB238 USB-C PD trigger (9 V): Adafruit HUSB238 USB-C power delivery trigger, 9 V pad bridged (1A and 5V traces cut).
  USB-C PD power bank 10 Ah: Kit power bank (10 Ah, PD, 2 USB outputs), strapped under the upper deck.
